# Fritzing sketch hogswatch (saved by Fritzing 0.9.2b)
circuit board: 6.88566cm x 5.36311cm
breadboards: 1
stripboards: 6

parts:
  Part1 = Arduino Uno (Rev3)
  LCD1 = LCD screen
  U1 = mystery part, 3 pins [chip_label=22L]
  U2 = mystery part, 3 pins [chip_label=22L]
  U3 = mystery part, 3 pins [chip_label=22L]
  U4 = mystery part, 3 pins [chip_label=22L]
  U5 = mystery part, 4 pins [chip_label=DHT22]
  U6 = mystery part, 4 pins [chip_label=DHT22]
  C1 = Ceramic Capacitor [capacitance=100nF package="100 mil [THT, multilayer]"]
  C2 = Ceramic Capacitor [capacitance=100nF package="100 mil [THT, multilayer]"]
  C3 = Ceramic Capacitor [capacitance=100nF package="100 mil [THT, multilayer]"]
  C4 = Ceramic Capacitor [capacitance=100nF package="100 mil [THT, multilayer]"]
  R1 = Resistor [tolerance=±5% resistance=10k package=THT]
  R2 = Resistor [tolerance=±5% resistance=10k package=THT]
  R3 = Resistor [tolerance=±5% resistance=10k package=THT]
  R4 = Resistor [tolerance=±5% resistance=10k package=THT]
  R5 = Resistor [tolerance=±5% resistance=10k package=THT]
  R6 = Resistor [tolerance=±5% resistance=10k package=THT]
  R7 = Rotary Potentiometer (Small) [maximum_resistance=100kΩ package=THT]
  Raspberry_Pi1 = Raspberry Pi B rev1
  Part2 = Logic Level Converter

nets:
  N1: Part1.A0, Part2.RX2_HV
  N2: Part1.A1, Part2.TX2_HV
  N3: Part1.A3, U6.pin2, R6.Pin_0
  N4: Part1.A5/SCL, U5.pin2, R5.Pin_0
  N5: Part1.D8, LCD1.RS
  N6: Part1.D9_PWM, LCD1.E
  N7: Part1.D10_PWM/SS, LCD1.DB4
  N8: Part1.D11_PWM/MOSI, LCD1.DB5
  N9: Part1.D12/MISO, LCD1.DB6
  N10: Part1.D13/SCK, LCD1.DB7
  N11: Part1.D2, U4.pin3, R4.Pin_0
  N12: Part1.D3_PWM, U3.pin3, R3.Pin_0
  N13: Part1.D6_PWM, U2.pin3, R2.Pin_0
  N14: Part1.D7, U1.pin3, R1.Pin_0
  5V: Part1.5V, LCD1.VDD, U1.pin1, U2.pin1, U3.pin1, U4.pin1, U5.pin1, U6.pin1, C1.0, C2.0, C3.0, C4.0, R1.Pin_1, R2.Pin_1, R3.Pin_1, R4.Pin_1, R5.Pin_1, R6.Pin_1, R7.leg1, Part2.HV
  GND: Part1.GND, LCD1.VSS, U1.pin2, U2.pin2, U3.pin2, U4.pin2, U5.pin4, U6.pin4, C1.1, C2.1, C3.1, C4.1, R7.leg2, Raspberry_Pi1.GND, Part2.GND
  N15: LCD1.V0, R7.wiper
  N16: Raspberry_Pi1.3V3, Part2.LV
  N17: Raspberry_Pi1.GPIO_14, Part2.TX2_LV
  N18: Raspberry_Pi1.GPIO_15, Part2.RX2_LV
